# Fritzing sketch IMU_sensor (saved by Fritzing 0.9.10b)

parts:
  M5Core-Ink = M5Core-Ink
  Part1 = InvenSense MPU6050

nets:
  5V: M5Core-Ink.1_5VIN
  3.3V: M5Core-Ink.2_3V3
  GND: M5Core-Ink.8_GND
  N1: M5Core-Ink.19_G22, Part1.SCL
  N2: M5Core-Ink.20_G21, Part1.SDA
  N3: M5Core-Ink.23_3V3, Part1.VCC
  N4: M5Core-Ink.28_GND, Part1.GND

notes:
  Microprocessor (ESP32)
  Inputs (Sensors)
  M5Stack Modules
  Outputs (Actuators)
  IMU(MPU6050)

custom parts:
  M5Core-Ink: M5Stack Core Ink ESP32 Board
